# Fritzing sketch Šema spajanja (saved by Fritzing 0.9.3b)
breadboards: 2

parts:
  Mod1 = Raspberry Pi Pico
  Mod2 = Raspberry Pi Pico
  DHT1 = Humidity and Temperature Sensor DHT11
  Part1 = FC-28 Soil Hygrometer Module - Probe
  부품3 = FC-28 Soil Hygrometer Module
  Water_Level_Sensor1 = Water Level Sensor
  D1 = LED_BARGRAPH_10 [package=led_bargaph_10]
  R1 = Resistor [tolerance=±5% resistance=220 package="0402 [SMD]"]
  R2 = Resistor [tolerance=±5% resistance=220 package="0402 [SMD]"]
  R3 = Resistor [tolerance=±5% resistance=220 package="0402 [SMD]"]
  R4 = Resistor [tolerance=±5% resistance=220 package="0402 [SMD]"]
  R5 = Resistor [tolerance=±5% resistance=220 package="0402 [SMD]"]
  R6 = Resistor [tolerance=±5% resistance=220 package="0402 [SMD]"]
  R7 = Resistor [tolerance=±5% resistance=220 package="0402 [SMD]"]
  R8 = Resistor [tolerance=±5% resistance=220 package="0402 [SMD]"]
  R9 = Resistor [tolerance=±5% resistance=220 package="0402 [SMD]"]
  R10 = Resistor [tolerance=±5% resistance=220 package="0402 [SMD]"]
  D2 = Diode [package=diode-1n4001]
  WATER_PUMP1 = water pump/motor
  Part2 = songle relay
  Q1 = NPN-Transistor [package="TO92 [THT]"]
  R11 = Resistor [tolerance=±5% resistance=1k package="2512 [SMD]"]
  LCD2 = TFT 1.8 inch 160x128 w SD

nets:
  N1: Mod1.pin_14, LCD2.pin_7
  N2: Mod1.pin_15, LCD2.pin_6
  N3: Mod1.pin_21, LCD2.pin_5
  N4: Mod1.pin_22, LCD2.pin4
  N5: Mod1.pin_24, LCD2.pin3
  N6: Mod1.pin_28, Mod1.pin_33, Mod1.pin_42, DHT1.GND_2, 부품3.GND, LCD2.pin2
  N7: Mod1.pin_31, DHT1.Data-signal
  N8: Mod1.pin_34, 부품3.AO
  VCC: Mod1.pin_36, DHT1.Vcc, 부품3.VCC, LCD2.pin_8
  N9: Mod1.pin_40, LCD2.pin_1
  N10: Mod2.pin_17, D1.J_A
  N11: Mod2.pin_19, D1.I_A
  N12: Mod2.pin_20, D1.H_A
  N13: Mod2.pin_21, D1.G_A
  N14: Mod2.pin_22, D1.F_A
  N15: Mod2.pin_24, D1.E_A
  N16: Mod2.pin_25, D1.D_A
  N17: Mod2.pin_26, D1.C_A
  N18: Mod2.pin_27, D1.B_A
  N19: Mod2.pin_29, D1.A_A
  N20: Mod2.pin_31, R11.Pin_1
  N21: Mod2.pin_33, Mod2.pin_38, Water_Level_Sensor1.GND, Q1.E
  N22: Mod2.pin_34, Water_Level_Sensor1.SIG
  VCC_2: Mod2.pin_36, Water_Level_Sensor1.VCC, Part2.VCC, Part2.COMMON
  N23: Part1.POS, 부품3.NEG
  N24: Part1.NEG, 부품3.POS
  N25: D1.J_C, R2.Pin_1
  N26: D1.I_C, R5.Pin_1
  N27: D1.H_C, R3.Pin_1
  N28: D1.G_C, R4.Pin_1
  N29: D1.F_C, R6.Pin_1
  N30: D1.E_C, R8.Pin_1
  N31: D1.D_C, R7.Pin_1
  N32: D1.C_C, R9.Pin_1
  N33: D1.B_C, R10.Pin_1
  N34: D1.A_C, R1.Pin_1
  N35: R1.Pin_0, R2.Pin_0, R3.Pin_0, R4.Pin_0, R5.Pin_0, R6.Pin_0, R7.Pin_0, R8.Pin_0, R9.Pin_0, R10.Pin_0, WATER_PUMP1.pin_1
  N36: D2.A, Part2.GND, Q1.B
  N37: WATER_PUMP1.pin_2, Part2.NO
  N38: Q1.C, R11.Pin_0

notes:
  pico1
  pico2

custom parts:
  Raspberry Pi Pico: Raspberry Pi Pico. Based around the RP2040 microcontroller the Pico is a low cost microcontroller device bringing Raspberry Pi quality, cost, and easy of use to the microcontroller space. Jan 2021, Split part in to two versions: tht (this one) and SMD. This one will drill holes for a .1 in header in pcb to allow plugging in the module as well as providing pads to solder the module to the top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
  Humidity and Temperature Sensor DHT11: Digital relative humidity & temperature sensor DHT11
  FC-28 Soil Hygrometer Module - Probe: The FC-28 is a soil hygrometer module that uses the Texas Instruments LM393 comparator chip to provide an analog measurement of soil humidity.
  FC-28 Soil Hygrometer Module: The FC-28 is a soil hygrometer module that uses the Texas Instruments LM393 comparator chip to provide an analog measurement of soil humidity. The digital output is high when soil moisture is over a certain threshold, as determined by adjusting the potentiometer.
  Water Level Sensor: A water level sensor. This sensor operates at 3V to 5V. The Sig (signal) pin outputs an analogue signal that is in proportion to the amount of water in contact with the sensor.
  water pump/motor: WATER PUMP BY ARDUBLOCKTR
  TFT 1.8 inch 160x128 w SD: This is a generic 1.8 tft spi lcd display available on ebay and others. The 1.8" display has 128x160 color pixels.
